# Fritzing sketch Exercise_3 (saved by Fritzing 0.9.3b)
breadboards: 1

parts:
  Componente1 = Arduino Uno (Rev3)
  LED1 = LED - 5mm [color="Red (633nm)" package="5 mm [THT]"]  # not connected
  R1 = Resistor [tolerance=±5% resistance=220 package=THT]  # not connected
  LED2 = LED - 5mm [color="Blue (430nm)" package="5 mm [THT]"]
  R2 = Resistor [tolerance=±5% resistance=220 package=THT]

nets:
  N1: Componente1.D3_PWM, LED2.anode
  N2: LED2.cathode, R2.Pin_1
