# Fritzing sketch Exercise_4 (saved by Fritzing 0.9.3b)
breadboards: 1

parts:
  Componente1 = Arduino Uno (Rev3)
  R1 = Resistor [tolerance=±5% resistance=10k package=THT]  # not connected
  LED2 = LED - 5mm [color="Red (633nm)" package="5 mm [THT]"]
  R2 = Resistor [tolerance=±5% resistance=220 package=THT]
  S1 = Pushbutton [package="[THT]"]

nets:
  N1: Componente1.D2, S1.Pin_3, S1.Pin_4
  N2: Componente1.D3_PWM, LED2.anode
  N3: Componente1.5V, S1.Pin_1, S1.Pin_2
  N4: LED2.cathode, R2.Pin_1
